# Fritzing sketch BeddoFabrik (saved by Fritzing 0.9.3b)

parts:
  Raspberry_Pi_Zero2 = Raspberry Pi Zero
  JP3 = Header 11 [package=1x11_smd_no_holes]
  JP4 = Header 11 [package=1x11_smd_no_holes]
  LAN_Reader_2 = RJ45
  LAN_Reader_1 = RJ45
  LAN_Reader_3 = RJ45
  LAN_Reader_4 = RJ45
  LAN_Reader_5 = RJ45
  Bauteil1 = RFID-RC522-v2
  Bauteil2 = RJ45
  Bauteil3 = RJ45  # not connected

nets:
  N1: Raspberry_Pi_Zero2.3v3, JP3.1, JP4.1, LAN_Reader_2.pin_1, LAN_Reader_1.pin_1, LAN_Reader_5.pin_1
  N2: Raspberry_Pi_Zero2.GPIO17, JP4.8, LAN_Reader_4.pin_7
  N3: Raspberry_Pi_Zero2.GPIO10, JP3.4, LAN_Reader_2.pin_4, LAN_Reader_1.pin_4
  N4: Raspberry_Pi_Zero2.GPIO9, JP3.3, LAN_Reader_2.pin_3, LAN_Reader_1.pin_3
  N5: Raspberry_Pi_Zero2.GPIO11, JP3.5, LAN_Reader_2.pin_5, LAN_Reader_1.pin_5
  N6: Raspberry_Pi_Zero2.GPIO5, JP4.11, LAN_Reader_3.pin_6
  N7: Raspberry_Pi_Zero2.GPIO6, JP4.9, LAN_Reader_4.pin_6
  N8: Raspberry_Pi_Zero2.GPIO13, JP4.7, LAN_Reader_5.pin_6
  N9: Raspberry_Pi_Zero2.GPIO19, JP4.5, LAN_Reader_5.pin_3
  N10: Raspberry_Pi_Zero2.GND, JP3.2, JP4.2, LAN_Reader_2.pin_2, LAN_Reader_1.pin_2, LAN_Reader_5.pin_2
  N11: Raspberry_Pi_Zero2.GPIO21, JP4.3, LAN_Reader_5.pin_5
  N12: Raspberry_Pi_Zero2.GPIO20, JP4.4, LAN_Reader_5.pin_4
  N13: Raspberry_Pi_Zero2.GPIO16, JP4.6, LAN_Reader_5.pin_7
  N14: Raspberry_Pi_Zero2.GPIO7, JP3.11, LAN_Reader_2.pin_7
  N15: Raspberry_Pi_Zero2.GPIO8, JP3.8, LAN_Reader_1.pin_7
  N16: Raspberry_Pi_Zero2.GPIO24, JP3.10, LAN_Reader_2.pin_6
  N17: Raspberry_Pi_Zero2.GPIO23, JP3.7, LAN_Reader_1.pin_6
  N18: Raspberry_Pi_Zero2.GPIO18, JP4.10, LAN_Reader_3.pin_7
  N19: Bauteil1.SDA, Bauteil2.pin_7
  N20: Bauteil1.SCK, Bauteil2.pin_5
  N21: Bauteil1.MOSI, Bauteil2.pin_4
  N22: Bauteil1.MISO, Bauteil2.pin_3
  N23: Bauteil1.GND, Bauteil2.pin_2
  N24: Bauteil1.RST, Bauteil2.pin_6
  N25: Bauteil1.3.3V, Bauteil2.pin_1

notes:
  SPI_0
  SPI_1
  RC522
  Reader_1
  Reader_2
  Reader_5
  Reader_3
  Reader_4
  +3.3V
  GND
  MISO
  MOSI
  SCLK
  RESET
  DATA

custom parts:
  RFID-RC522-v2: A simple China made RFID-RC522 Reader; do check the pin labels, as this is a MFRC522 based clone.
